// Logisim project cpu.circ as structural Verilog: 1 circuit, main circuit main
module main (
  input  [31:0] INSTRUCTION,
  input  CLOCK,
  output [31:0] PROGRAM_COUNTER,
  output [31:0] ra,
  output [31:0] sp,
  output [31:0] t0,
  output [31:0] t1,
  output [31:0] t2,
  output [31:0] s0,
  output [31:0] s1,
  output [31:0] a0
);

  wire control_logic_1_regwen;
  wire [1:0] control_logic_1_wbsel;
  wire [3:0] control_logic_1_alusel;
  wire [31:0] adder_1_out, alu_out, imm_out, RegFile_read_data_1;

  control_logic control_logic_1 (
    .RegWEn(control_logic_1_regwen), .ALUSel(control_logic_1_alusel), .WBSel(control_logic_1_wbsel));  // open: BSel, BrUn, ImmSel, ASel, PCSel, BrLt, BrEq, inst, MemRW
  Adder #(.width(32)) adder_1 (.a(PROGRAM_COUNTER), .b(32'h4), .out(adder_1_out));  // open: cin, cout
  Register #(.width(32)) PC (.D(adder_1_out), .clk(CLOCK), .Q(PROGRAM_COUNTER));  // open: en, clr
  imm_gen imm_gen_1 (.inst(INSTRUCTION), .imm(imm_out));  // open: ImmSel
  // branch_comp branch_comp_1: pin names not known
  regfile_main RegFile (
    .rs2(INSTRUCTION[24:20]), .rd(INSTRUCTION[11:7]), .Read_Data_1(RegFile_read_data_1), .ra(ra), .sp(sp),
    .t0(t0), .t1(t1), .t2(t2), .s0(s0), .s1(s1), .a0(a0), .rs1(INSTRUCTION[19:15]), .Write_Data(alu_out),
    .RegWEn(control_logic_1_regwen), .clk(CLOCK));  // open: Read_Data_2, in_7
  alu Arithmetic_Logic_Unit (
    .Result(alu_out), .ALUSel(control_logic_1_alusel), .A(RegFile_read_data_1), .B(imm_out));  // open: in_2, in_4
  // mem_main DMEM: pin names not known
  Multiplexer #(.select(2), .width(32), .enable("false")) multiplexer_1 (
    .in0(alu_out), .sel(control_logic_1_wbsel));  // open: in1, in2, in3, out

  // Other names for the same wires on the sheet: clk = CLOCK; i_0_6_op[6:0] = INSTRUCTION[6:0];
  //   i_7_11_rd[4:0] = INSTRUCTION[11:7]; i_12_14_func3[2:0] = INSTRUCTION[14:12];
  //   i_15_19_rs1[4:0] = INSTRUCTION[19:15]; i_20_24_rs2[4:0] = INSTRUCTION[24:20];
  //   i_25_31_func7[6:0] = INSTRUCTION[31:25]

  // Notes on the sheet:
  //   Output
  //   IMEM (do **NOT** move this)
  //   Inputs
  //   Inputs/Outputs for testing. Do **NOT** move these.
endmodule
